// Logisim project Atraso.circ as structural Verilog: 1 circuit, main circuit main
module main (
);

  wire and_1_out, button_1_out, not_1_out, not_2_out, not_3_out, not_4_out, not_5_out;

  Button button_1 (.out(button_1_out));
  not not_1 (not_1_out, button_1_out);
  not not_2 (not_2_out, not_1_out);
  not not_3 (not_3_out, not_4_out);
  not not_4 (not_4_out, not_2_out);
  not not_5 (not_5_out, not_3_out);
  and and_1 (and_1_out, button_1_out, not_5_out);
  LED led_1 (.in(and_1_out));
endmodule
