// Logisim project Porta_AND.circ as structural Verilog: 1 circuit, main circuit main
module main (
);

  wire not_1_out, not_2_out, not_3_out, or_1_out, undriven, undriven_2;

  not not_1 (not_1_out, undriven);
  not not_2 (not_2_out, undriven_2);
  or or_1 (or_1_out, not_1_out, not_2_out);
  not not_3 (not_3_out, or_1_out);

  // Notes on the sheet:
  //   A
  //   B
endmodule
