// Logisim project Teste_LED.circ as structural Verilog: 1 circuit, main circuit main
module main (
);

  wire button_1_out, not_1_out;

  Button button_1 (.out(button_1_out));
  not not_1 (not_1_out, button_1_out);
  LED led_1 (.in(not_1_out));
endmodule
