// Logisim project Funcao_XOR.circ as structural Verilog: 1 circuit, main circuit main
module main (
);

  wire nand_1_out, nand_2_out, nand_4_out, undriven, undriven_2;

  nand nand_1 (nand_1_out, undriven_2, undriven);
  nand nand_2 (nand_2_out, undriven_2, nand_1_out);
  nand nand_3 (nand_2_out, nand_1_out, undriven);
  not nand_4 (nand_4_out, nand_2_out);  // NAND_Gate

  // Notes on the sheet:
  //   A
  //   B
  //   !AB + A!B = A^B
endmodule
