// Logisim project circ_maioria.circ as structural Verilog: 1 circuit, main circuit main
module main (
  input  A,
  input  B,
  input  C,
  input  D
);

  wire and_1_out, and_2_out, and_3_out, and_4_out, or_1_out, or_2_out, or_3_out;

  and and_1 (and_1_out, A, B);
  or or_1 (or_1_out, C, D);
  and and_2 (and_2_out, C, D);
  or or_2 (or_2_out, A, B);
  and and_3 (and_3_out, and_1_out, or_1_out);
  and and_4 (and_4_out, and_2_out, or_2_out);
  or or_3 (or_3_out, and_3_out, and_4_out);
  LED led_1 (.in(or_3_out));

  // Notes on the sheet:
  //   X
endmodule
