// Logisim project Porta_NAND_3_entradas.circ as structural Verilog: 1 circuit, main circuit main
module main (
);

  wire nand_1_out, nand_2_out, nand_3_out, undriven, undriven_2, undriven_3;

  nand nand_1 (nand_1_out, undriven, undriven_2);
  nand nand_2 (nand_2_out, nand_1_out, nand_1_out);
  nand nand_3 (nand_3_out, nand_2_out, undriven_3);

  // Notes on the sheet:
  //   A
  //   B
  //   C
  //   !(ABC)
endmodule
